# Fritzing sketch Wiring Schematic (saved by Fritzing 0.6.3b)
breadboards: 1

parts:
  U1 = Arduino Mega
  Part1 = Thumb Joystick
  S1 = Pushbutton [package="[THT]"]
  LED1 = LED - 5mm [color="Red (633nm)" package="5 mm [THT]"]
  R1 = Resistor [tolerance=±5% resistance=220 package="0805 [SMD]"]
  R2 = Resistor [tolerance=±5% resistance=220 package="0805 [SMD]"]

nets:
  N1: U1.D13, R2.Pin_0
  N2: U1.D12, R1.Pin_0
  N3: U1.D11, Part1.SEL
  N4: U1.A0, Part1.HORZ
  N5: U1.A1, Part1.VERT
  N6: Part1.GND, S1.Pin_1, S1.Pin_2, LED1.cathode
  N7: S1.Pin_3, S1.Pin_4, R1.Pin_1
  N8: LED1.anode, R2.Pin_1
